// Logisim project tsc8.circ as structural Verilog: 5 circuits, main circuit main
module main (
);

  wire and_1_out, and_2_out, and_3_out, and_4_out, and_5_out, and_6_out, and_7_out, and_8_out, and_9_out,
       button_1_out, clock_1_out, comparator_1_eq, comparator_2_eq, controlled_buffer_5_out, not_1_out,
       not_2_out, not_3_out, not_4_out, not_5_out, not_6_out, not_7_out, or_1_out, switch_1_p2, switch_2_p2,
       w65c02s_simple_1_p5;
  wire [6:0] controlled_buffer_3_out, keyboard_1_data;
  wire [7:0] controlled_buffer_10_out, ram_1_dout, rom_1_data, switch_18_p2, w65c02s_simple_1_p6;
  wire [7:7] controlled_buffer_3_out_2;
  wire [15:0] controlled_buffer_1_out, switch_25_p2, w65c02s_simple_1_p7;

  Button button_1 (.out(button_1_out));
  not not_1 (not_1_out, button_1_out);
  // Switch switch_1: pin names not known; wires that end beside it: 1'b1, switch_1_p2
  Clock clock_1 (.out(clock_1_out));
  and and_1 (and_1_out, 1'b1, not_1_out);
  Pull_Resistor pull_resistor_1 (.node(switch_1_p2));
  // Switch switch_2: pin names not known; wires that end beside it: 1'b1, switch_2_p2
  Pull_Resistor pull_resistor_2 (.node(switch_2_p2));
  and and_2 (and_2_out, clock_1_out, switch_1_p2);
  LED led_1 (.in(controlled_buffer_1_out[15]));
  LED led_2 (.in(controlled_buffer_1_out[14]));
  LED led_3 (.in(controlled_buffer_1_out[13]));
  LED led_4 (.in(controlled_buffer_3_out_2[7]));
  LED led_5 (.in(controlled_buffer_3_out[6]));
  LED led_6 (.in(controlled_buffer_3_out[5]));
  // Switch switch_3: pin names not known; wires that end beside it: 1'b1, switch_25_p2[15]
  Pull_Resistor pull_resistor_3 (.node(switch_25_p2[15]));
  // Switch switch_4: pin names not known; wires that end beside it: 1'b1, switch_18_p2[7], switch_18_p2[7]
  Pull_Resistor pull_resistor_4 (.node(switch_18_p2[7]));
  LED led_7 (.in(controlled_buffer_1_out[12]));
  LED led_8 (.in(controlled_buffer_1_out[11]));
  LED led_9 (.in(controlled_buffer_1_out[10]));
  LED led_10 (.in(controlled_buffer_1_out[9]));
  LED led_11 (.in(controlled_buffer_3_out[4]));
  LED led_12 (.in(controlled_buffer_3_out[3]));
  LED led_13 (.in(controlled_buffer_3_out[2]));
  LED led_14 (.in(controlled_buffer_3_out[1]));
  // Switch switch_5: pin names not known; wires that end beside it: 1'b1, switch_25_p2[14]
  // Switch switch_6: pin names not known; wires that end beside it: 1'b1, switch_25_p2[13]
  Pull_Resistor pull_resistor_5 (.node(switch_25_p2[14]));
  Pull_Resistor pull_resistor_6 (.node(switch_25_p2[13]));
  // Switch switch_7: pin names not known; wires that end beside it: 1'b1, switch_18_p2[6], switch_18_p2[6]
  // Switch switch_8: pin names not known; wires that end beside it: 1'b1, switch_18_p2[5], switch_18_p2[5]
  Pull_Resistor pull_resistor_7 (.node(switch_18_p2[6]));
  Pull_Resistor pull_resistor_8 (.node(switch_18_p2[5]));
  // W65C02S__Simple w65c02s_simple_1: pin names not known; wires that end beside it: and_2_out, 1'b0, 1'b0, and_1_out, w65c02s_simple_1_p5, w65c02s_simple_1_p6, w65c02s_simple_1_p7
  LED led_15 (.in(controlled_buffer_1_out[8]));
  LED led_16 (.in(controlled_buffer_1_out[7]));
  LED led_17 (.in(controlled_buffer_1_out[6]));
  LED led_18 (.in(controlled_buffer_1_out[5]));
  LED led_19 (.in(controlled_buffer_3_out[0]));
  // Switch switch_9: pin names not known; wires that end beside it: 1'b1, switch_25_p2[12]
  Pull_Resistor pull_resistor_9 (.node(switch_25_p2[12]));
  // Switch switch_10: pin names not known; wires that end beside it: 1'b1, switch_18_p2[4], switch_18_p2[4]
  Pull_Resistor pull_resistor_10 (.node(switch_18_p2[4]));
  LED led_20 (.in(controlled_buffer_1_out[4]));
  LED led_21 (.in(controlled_buffer_1_out[3]));
  LED led_22 (.in(controlled_buffer_1_out[2]));
  LED led_23 (.in(controlled_buffer_1_out[1]));
  // Switch switch_11: pin names not known; wires that end beside it: 1'b1, switch_25_p2[11]
  // Switch switch_12: pin names not known; wires that end beside it: 1'b1, switch_25_p2[10]
  Pull_Resistor pull_resistor_11 (.node(switch_25_p2[11]));
  Pull_Resistor pull_resistor_12 (.node(switch_25_p2[10]));
  // Switch switch_13: pin names not known; wires that end beside it: 1'b1, switch_18_p2[3], switch_18_p2[3]
  // Switch switch_14: pin names not known; wires that end beside it: 1'b1, switch_18_p2[2], switch_18_p2[2]
  Pull_Resistor pull_resistor_13 (.node(switch_18_p2[3]));
  Pull_Resistor pull_resistor_14 (.node(switch_18_p2[2]));
  and and_3 (and_3_out, not_2_out, switch_1_p2);
  not not_2 (not_2_out, w65c02s_simple_1_p5);
  assign controlled_buffer_1_out = switch_1_p2 ? w65c02s_simple_1_p7 : 16'bz;  // Controlled_Buffer controlled_buffer_1
  assign w65c02s_simple_1_p6 = w65c02s_simple_1_p5 ? {controlled_buffer_3_out_2[7], controlled_buffer_3_out} : 8'bz;  // Controlled_Buffer controlled_buffer_2
  LED led_24 (.in(controlled_buffer_1_out[0]));
  not not_3 (not_3_out, switch_1_p2);
  // Switch switch_15: pin names not known; wires that end beside it: 1'b1, switch_25_p2[9]
  // Switch switch_16: pin names not known; wires that end beside it: 1'b1, switch_25_p2[8]
  Pull_Resistor pull_resistor_15 (.node(switch_25_p2[9]));
  // Switch switch_17: pin names not known; wires that end beside it: 1'b1, switch_18_p2[1], switch_18_p2[1]
  // Switch switch_18: pin names not known; wires that end beside it: 1'b1, switch_18_p2[0], switch_18_p2[0]
  Pull_Resistor pull_resistor_16 (.node(switch_18_p2[1]));
  assign {controlled_buffer_3_out_2[7], controlled_buffer_3_out} = and_3_out ? w65c02s_simple_1_p6 : 8'bz;  // Controlled_Buffer controlled_buffer_3
  not not_4 (not_4_out, switch_1_p2);
  assign controlled_buffer_1_out = not_3_out ? switch_25_p2 : 16'bz;  // Controlled_Buffer controlled_buffer_4
  // Switch switch_19: pin names not known; wires that end beside it: 1'b1, switch_25_p2[7]
  Pull_Resistor pull_resistor_17 (.node(switch_25_p2[8]));
  Pull_Resistor pull_resistor_18 (.node(switch_25_p2[7]));
  Pull_Resistor pull_resistor_19 (.node(switch_18_p2[0]));
  assign controlled_buffer_5_out = switch_1_p2 ? w65c02s_simple_1_p5 : 1'bz;  // Controlled_Buffer controlled_buffer_5
  assign controlled_buffer_5_out = not_4_out ? not_5_out : 1'bz;  // Controlled_Buffer controlled_buffer_6
  not not_5 (not_5_out, switch_2_p2);
  // Switch switch_20: pin names not known; wires that end beside it: 1'b1, switch_25_p2[6]
  // Switch switch_21: pin names not known; wires that end beside it: 1'b1, switch_25_p2[5]
  Pull_Resistor pull_resistor_20 (.node(switch_25_p2[6]));
  Pull_Resistor pull_resistor_21 (.node(switch_25_p2[5]));
  // Switch switch_22: pin names not known; wires that end beside it: 1'b1, switch_25_p2[4]
  Pull_Resistor pull_resistor_22 (.node(switch_25_p2[4]));
  or or_1 (or_1_out, controlled_buffer_1_out[15], controlled_buffer_1_out[14], controlled_buffer_1_out[13]);
  and and_4 (and_4_out, controlled_buffer_1_out[15], controlled_buffer_1_out[14], controlled_buffer_1_out[13]);
  not not_6 (not_6_out, or_1_out);
  and and_5 (and_5_out, not_6_out, controlled_buffer_5_out);
  and and_6 (and_6_out, not_6_out, not_7_out);
  not not_7 (not_7_out, controlled_buffer_5_out);
  // Switch switch_23: pin names not known; wires that end beside it: 1'b1, switch_25_p2[3]
  // Switch switch_24: pin names not known; wires that end beside it: 1'b1, switch_25_p2[2]
  Pull_Resistor pull_resistor_23 (.node(switch_25_p2[3]));
  Pull_Resistor pull_resistor_24 (.node(switch_25_p2[2]));
  assign {controlled_buffer_3_out_2[7], controlled_buffer_3_out} = switch_1_p2 ? controlled_buffer_10_out : 8'bz;  // Controlled_Buffer controlled_buffer_7
  RAM #(.addrWidth(15)) ram_1 (
    .addr(controlled_buffer_1_out[14:0]), .we(and_6_out), .oe(and_5_out), .clk(clock_1_out),
    .din({controlled_buffer_3_out_2[7], controlled_buffer_3_out}), .dout(ram_1_dout));
  ROM #(.addrWidth(13)) rom_1 (.addr(controlled_buffer_1_out[12:0]), .data(rom_1_data));
  Comparator #(.width(16)) comparator_1 (
    .a(controlled_buffer_1_out), .b(16'h8000), .eq(comparator_1_eq));  // open: gt, lt
  Comparator #(.width(16)) comparator_2 (
    .a(controlled_buffer_1_out), .b(16'h8001), .eq(comparator_2_eq));  // open: gt, lt
  // Switch switch_25: pin names not known; wires that end beside it: 1'b1, switch_25_p2[0]
  // Switch switch_26: pin names not known; wires that end beside it: 1'b1, switch_25_p2[1]
  Pull_Resistor pull_resistor_25 (.node(switch_25_p2[1]));
  and and_7 (and_7_out, controlled_buffer_5_out, comparator_2_eq);
  assign {controlled_buffer_3_out_2[7], controlled_buffer_3_out} = not_3_out ? switch_18_p2 : 8'bz;  // Controlled_Buffer controlled_buffer_8
  Pull_Resistor pull_resistor_26 (.node(switch_25_p2[0]));
  and and_8 (and_8_out, comparator_1_eq, not_7_out);
  and and_9 (and_9_out, and_4_out, controlled_buffer_5_out);
  Keyboard #(.trigger("falling")) keyboard_1 (
    .clk(clock_1_out), .re(and_7_out), .data(keyboard_1_data));  // open: clr, avail
  assign {controlled_buffer_3_out_2[7], controlled_buffer_3_out} = and_7_out ? {1'b0, keyboard_1_data} : 8'bz;  // Controlled_Buffer controlled_buffer_9
  TTY #(.cols(80), .rows(25)) tty_1 (.data(controlled_buffer_3_out), .clk(clock_1_out), .we(and_8_out));  // open: clr
  assign controlled_buffer_10_out = and_5_out ? ram_1_dout : 8'bz;  // Controlled_Buffer controlled_buffer_10
  assign controlled_buffer_10_out = and_9_out ? rom_1_data : 8'bz;  // Controlled_Buffer controlled_buffer_11

  // Notes on the sheet:
  //   Enable CPU
  //   Enable Write
  //   Address
  //   Data
  //   contents of rom_1 (hex, n*v repeats v):
  //   a9 8b 85 2 a9 e2 85 3 20 e e0 4c 1c e0 a0 0 b1 2 f0 7 8d 0 80 c8 4c 10 e0 60 20 7e e2 a9 0 a9 3f 8d
  //   0 80 a0 0 ad 1 80 f0 fb c9 a f0 1c c9 8 f0 e 99 4 0 8d 0 80 c8 c0 30 f0 dc 4c 28 e0 8d 0 80 88 10 df
  //   c8 4c 28 e0 8d 0 80 a0 0 20 79 e2 c9 20 f0 f9 c9 72 f0 f c9 77 f0 53 c9 65 f0 79 c9 68 f0 7b 4c 1c
  //   e0 20 bf e1 a9 1 85 3d a5 35 85 3b a5 36 85 3c e0 0 f0 7 20 bf e1 a5 35 85 3d a0 0 b1 3b aa 98 48 8a
  //   20 23 e2 aa 68 a8 8a c8 98 29 f d0 8 a9 a 8d 0 80 4c a8 e0 a9 20 8d 0 80 c4 3d d0 dc a9 a 8d 0 80 4c
  //   1c e0 20 bf e1 e0 0 d0 3 4c 1c e0 a5 35 85 3b a5 36 85 3c 84 3d a4 3d 20 bf e1 84 3d a0 0 a5 35 91
  //   3b e6 3b e0 0 d0 ed 4c 1c e0 20 bf e1 6c 35 0 a2 0 bd f5 e0 f0 7 8d 0 80 e8 4c e6 e0 4c 1c e0 48 6f
  //   77 20 74 6f 20 75 73 65 20 74 68 65 20 6d 6f 6e 69 74 6f 72 3a d a 20 20 2a 20 72 20 3c 61 64 64 72
  //   3e 20 5b 6e 5d 3a 20 50 72 69 6e 74 20 5b 6e 5d 20 62 79 74 65 73 20 66 72 6f 6d 20 3c 61 64 64 72
  //   3e d a 20 20 2a 20 77 20 3c 61 64 64 72 3e 20 5b 64 61 74 5d 3a 20 57 72 69 74 65 20 5b 64 61 74 5d
  //   20 74 6f 20 3c 61 64 64 72 3e d a 20 20 2a 20 65 20 3c 61 64 64 72 3e 3a 20 53 74 61 72 74 20 65 78
  //   65 63 75 74 69 6f 6e 20 61 74 20 3c 61 64 64 72 3e d a a 41 6c 6c 20 76 61 6c 75 65 73 20 6d 75 73
  //   74 20 62 65 20 77 72 69 74 74 65 6e 20 69 6e 20 68 65 78 61 64 65 63 69 6d 61 6c 2e d a 0 a9 0 85 35
  //   85 36 b9 4 0 c9 20 d0 6 20 79 e2 4c bf e1 a9 0 a2 0 20 79 e2 c9 0 f0 42 c9 20 f0 3c c9 30 30 3b f0 9
  //   c9 61 30 17 f0 8 4c fa e1 a9 0 4c 5 e2 a9 a 4c 5 e2 18 e9 61 69 a 4c 5 e2 38 e9 30 6 35 26 36 6 35
  //   26 36 6 35 26 36 6 35 26 36 18 5 35 85 35 4c d2 e1 a2 1 60 4c 1c e0 a2 1 a0 0 84 3a 84 37 84 38 c9 0
  //   f0 3f 4a 66 3a 4a 66 3a 4a 66 3a 4a 66 3a 18 66 3a 66 3a 66 3a 66 3a 18 a8 a5 3a c9 a 30 8 e9 a 18
  //   69 41 4c 58 e2 69 30 95 37 a9 0 85 3a ca 98 e0 ff d0 cd a9 37 85 2 a9 0 85 3 20 e e0 60 a9 30 8d 0
  //   80 8d 0 80 60 b9 4 0 c8 60 a0 0 a9 0 99 4 0 c8 c0 30 d0 f8 60 54 53 43 2d 38 20 52 4f 4d 20 76 30 2e
  //   31 20 4d 4c 20 4d 6f 6e 69 74 6f 72 2e d a 54 79 70 65 20 27 68 27 20 74 68 65 6e 20 65 6e 74 65 72
  //   20 66 6f 72 20 61 20 6c 69 73 74 20 6f 66 20 63 6f 6d 6d 61 6e 64 73 2e d a 7465*0 e0
endmodule

module breadboard (
);

  wire and_1_out, and_2_out, button_1_out, clock_1_out, comparator_1_eq, comparator_2_eq, n7400_1_pin11,
       n7400_2_pin3, n7408_1_pin3, n7408_1_pin6, not_1_out, w65c02s_pdip_40_1_p1, w65c02s_pdip_40_1_p17,
       w65c02s_pdip_40_1_p20, w65c02s_pdip_40_1_p33;
  wire [3:0] w65c02s_pdip_40_1_p5, w65c02s_pdip_40_1_p9, w65c02s_pdip_40_1_p13, w65c02s_pdip_40_1_p32;
  wire [6:0] keyboard_1_data;
  wire [7:0] w65c02s_pdip_40_1_p21;

  Clock clock_1 (.out(clock_1_out));
  Button button_1 (.out(button_1_out));
  // W65C02S__PDIP_40 w65c02s_pdip_40_1: pin names not known; wires that end beside it: w65c02s_pdip_40_1_p1, w65c02s_pdip_40_1_p1, w65c02s_pdip_40_1_p1, w65c02s_pdip_40_1_p1, w65c02s_pdip_40_1_p5[0], w65c02s_pdip_40_1_p5[1], w65c02s_pdip_40_1_p5[2], w65c02s_pdip_40_1_p5[3], w65c02s_pdip_40_1_p9[0], w65c02s_pdip_40_1_p9[1], w65c02s_pdip_40_1_p9[2], w65c02s_pdip_40_1_p9[3], w65c02s_pdip_40_1_p13[0], w65c02s_pdip_40_1_p13[1], w65c02s_pdip_40_1_p13[2], w65c02s_pdip_40_1_p13[3], w65c02s_pdip_40_1_p17, clock_1_out, w65c02s_pdip_40_1_p1, w65c02s_pdip_40_1_p20, w65c02s_pdip_40_1_p21[0], w65c02s_pdip_40_1_p21[1], w65c02s_pdip_40_1_p21[2], w65c02s_pdip_40_1_p21[3], w65c02s_pdip_40_1_p21[4], w65c02s_pdip_40_1_p21[5], w65c02s_pdip_40_1_p21[6], w65c02s_pdip_40_1_p21[7], w65c02s_pdip_40_1_p32[3], w65c02s_pdip_40_1_p32[2], w65c02s_pdip_40_1_p32[1], w65c02s_pdip_40_1_p32[0], w65c02s_pdip_40_1_p33
  _7400 #(.ShowInternalStructure("true"), .VccGndPorts("true")) u_7400_1 (
    .pin1(button_1_out), .pin2(button_1_out), .pin3(w65c02s_pdip_40_1_p17), .pin7(w65c02s_pdip_40_1_p33),
    .pin14(w65c02s_pdip_40_1_p1), .pin13(w65c02s_pdip_40_1_p20), .pin12(w65c02s_pdip_40_1_p20),
    .pin11(n7400_1_pin11));  // open: pin4, pin5, pin6, pin10, pin9, pin8
  romic romic_1 (
    .a0(w65c02s_pdip_40_1_p5[0]), .a1(w65c02s_pdip_40_1_p5[1]), .a2(w65c02s_pdip_40_1_p5[2]),
    .a3(w65c02s_pdip_40_1_p5[3]), .a4(w65c02s_pdip_40_1_p9[0]), .a5(w65c02s_pdip_40_1_p9[1]),
    .a6(w65c02s_pdip_40_1_p9[2]), .a7(w65c02s_pdip_40_1_p9[3]), .a8(w65c02s_pdip_40_1_p13[0]),
    .a9(w65c02s_pdip_40_1_p13[1]), .a10(w65c02s_pdip_40_1_p13[2]), .a11(w65c02s_pdip_40_1_p13[3]),
    .a12(w65c02s_pdip_40_1_p32[0]), .vcc(w65c02s_pdip_40_1_p1), .gnd(w65c02s_pdip_40_1_p33),
    .we(w65c02s_pdip_40_1_p1), .oe(n7400_1_pin11), .ce(n7400_2_pin3), .io0(w65c02s_pdip_40_1_p21[0]),
    .io1(w65c02s_pdip_40_1_p21[1]), .io2(w65c02s_pdip_40_1_p21[2]), .io3(w65c02s_pdip_40_1_p21[3]),
    .io4(w65c02s_pdip_40_1_p21[4]), .io5(w65c02s_pdip_40_1_p21[5]), .io6(w65c02s_pdip_40_1_p21[6]),
    .io7(w65c02s_pdip_40_1_p21[7]));
  nvram nvram_1 (
    .a0(w65c02s_pdip_40_1_p5[0]), .a1(w65c02s_pdip_40_1_p5[1]), .a2(w65c02s_pdip_40_1_p5[2]),
    .a3(w65c02s_pdip_40_1_p5[3]), .a4(w65c02s_pdip_40_1_p9[0]), .a5(w65c02s_pdip_40_1_p9[1]),
    .a6(w65c02s_pdip_40_1_p9[2]), .a7(w65c02s_pdip_40_1_p9[3]), .a8(w65c02s_pdip_40_1_p13[1]),
    .a9(w65c02s_pdip_40_1_p13[0]), .a10(w65c02s_pdip_40_1_p13[2]), .a11(w65c02s_pdip_40_1_p13[3]),
    .a12(w65c02s_pdip_40_1_p32[0]), .a13(w65c02s_pdip_40_1_p32[1]), .a14(w65c02s_pdip_40_1_p32[2]),
    .VCC(w65c02s_pdip_40_1_p1), .VSS(w65c02s_pdip_40_1_p33), .E(w65c02s_pdip_40_1_p32[3]),
    .W(w65c02s_pdip_40_1_p20), .G(n7400_1_pin11), .C(clock_1_out), .D(w65c02s_pdip_40_1_p21),
    .DQ0(w65c02s_pdip_40_1_p21[0]), .DQ1(w65c02s_pdip_40_1_p21[1]), .DQ2(w65c02s_pdip_40_1_p21[2]),
    .DQ3(w65c02s_pdip_40_1_p21[3]), .DQ4(w65c02s_pdip_40_1_p21[4]), .DQ5(w65c02s_pdip_40_1_p21[5]),
    .DQ6(w65c02s_pdip_40_1_p21[6]), .DQ7(w65c02s_pdip_40_1_p21[7]));
  _7408 #(.ShowInternalStructure("true"), .VccGndPorts("true")) u_7408_1 (
    .pin1(w65c02s_pdip_40_1_p32[3]), .pin2(w65c02s_pdip_40_1_p32[2]), .pin3(n7408_1_pin3),
    .pin4(n7408_1_pin3), .pin5(w65c02s_pdip_40_1_p32[1]), .pin6(n7408_1_pin6), .pin7(w65c02s_pdip_40_1_p33),
    .pin14(w65c02s_pdip_40_1_p1));  // open: pin13, pin12, pin11, pin10, pin9, pin8
  _7400 #(.ShowInternalStructure("true"), .VccGndPorts("true")) u_7400_2 (
    .pin1(n7408_1_pin6), .pin2(n7408_1_pin6), .pin3(n7400_2_pin3), .pin7(w65c02s_pdip_40_1_p33),
    .pin14(w65c02s_pdip_40_1_p1));  // open: pin4, pin5, pin6, pin13, pin12, pin11, pin10, pin9, pin8
  TTY #(.cols(80), .rows(25)) tty_1 (
    .data(w65c02s_pdip_40_1_p21[6:0]), .clk(clock_1_out), .we(and_2_out));  // open: clr
  Comparator #(.width(16)) comparator_1 (
    .a({w65c02s_pdip_40_1_p32, w65c02s_pdip_40_1_p13, w65c02s_pdip_40_1_p9, w65c02s_pdip_40_1_p5}),
    .b(16'h8001), .eq(comparator_1_eq));  // open: gt, lt
  Comparator #(.width(16)) comparator_2 (
    .a({w65c02s_pdip_40_1_p32, w65c02s_pdip_40_1_p13, w65c02s_pdip_40_1_p9, w65c02s_pdip_40_1_p5}),
    .b(16'h8000), .eq(comparator_2_eq));  // open: gt, lt
  not not_1 (not_1_out, w65c02s_pdip_40_1_p20);
  and and_1 (and_1_out, comparator_1_eq, w65c02s_pdip_40_1_p20);
  and and_2 (and_2_out, comparator_2_eq, not_1_out);
  Keyboard #(.trigger("falling")) keyboard_1 (
    .clk(clock_1_out), .re(and_1_out), .data(keyboard_1_data));  // open: clr, avail
  assign w65c02s_pdip_40_1_p21 = and_1_out ? {1'b0, keyboard_1_data} : 8'bz;  // Controlled_Buffer controlled_buffer_1
  Hex_Digit_Display hex_digit_display_1 (.value(w65c02s_pdip_40_1_p32));  // open: dp
  Hex_Digit_Display hex_digit_display_2 (.value(w65c02s_pdip_40_1_p13));  // open: dp
  Hex_Digit_Display hex_digit_display_3 (.value(w65c02s_pdip_40_1_p9));  // open: dp
  Hex_Digit_Display hex_digit_display_4 (.value(w65c02s_pdip_40_1_p5));  // open: dp
  // also tied to GND on the sheet: w65c02s_pdip_40_1_p33
  // also tied to VCC on the sheet: w65c02s_pdip_40_1_p1
endmodule

module ics (
  input  CPUEn
);

  wire CLK, hi, lo, n7400_2_pin3, n7408_1_pin3, n7408_1_pin9, n7408_1_pin11, n7408_1_pin12, n7408_2_pin3,
       n7408_2_pin6, n7408_3_pin3, n7408_3_pin6, n7408_4_pin3, RAM_CS, RD, ROM_CS, RSB, TTYCS, WR;
  wire [6:0] keyboard_1_data;
  wire [7:0] D, ram_1_dout, rom_1_data;
  wire [15:0] A;

  Clock clock_1 (.out(CLK));
  _7408 #(.ShowInternalStructure("true"), .VccGndPorts("true")) u_7408_1 (
    .pin1(A[13]), .pin2(A[14]), .pin3(n7408_1_pin3), .pin4(n7408_1_pin3), .pin5(A[15]), .pin6(ROM_CS),
    .pin7(lo), .pin14(hi), .pin13(A[15]), .pin12(n7408_1_pin12), .pin11(n7408_1_pin11),
    .pin10(n7408_1_pin11), .pin9(n7408_1_pin9), .pin8(TTYCS));
  _7400 #(.ShowInternalStructure("true"), .VccGndPorts("true")) u_7400_1 (
    .pin1(A[14]), .pin2(A[14]), .pin3(n7408_1_pin12), .pin4(A[15]), .pin5(A[15]), .pin6(RAM_CS), .pin7(lo),
    .pin14(hi), .pin13(A[13]), .pin12(A[13]), .pin11(n7408_1_pin9));  // open: pin10, pin9, pin8
  // W65C02S__PDIP_40 w65c02s_pdip_40_1: pin names not known; wires that end beside it: CPUEn, hi, hi, hi, A[0], A[1], A[2], A[3], A[4], A[5], A[6], A[7], A[8], A[9], A[10], A[11], RSB, CLK, CPUEn, RD, A[15], A[14], A[13], A[12], lo
  Button #(.press("passive")) button_1 (.out(RSB));
  TTY #(.cols(80), .rows(25)) tty_1 (.data(D[6:0]), .clk(CLK), .we(n7408_2_pin3), .clr(n7400_2_pin3));
  _7408 #(.ShowInternalStructure("true"), .VccGndPorts("true")) u_7408_2 (
    .pin1(TTYCS), .pin2(WR), .pin3(n7408_2_pin3), .pin4(TTYCS), .pin5(RD), .pin6(n7408_2_pin6), .pin7(lo),
    .pin14(hi));  // open: pin13, pin12, pin11, pin10, pin9, pin8
  _7400 #(.ShowInternalStructure("true"), .VccGndPorts("true")) u_7400_2 (
    .pin1(RSB), .pin2(RSB), .pin3(n7400_2_pin3), .pin7(lo), .pin14(hi));  // open: pin4, pin5, pin6, pin13, pin12, pin11, pin10, pin9, pin8
  _7400 #(.ShowInternalStructure("true"), .VccGndPorts("true")) u_7400_3 (
    .pin1(RD), .pin2(RD), .pin3(WR), .pin7(lo), .pin14(hi));  // open: pin4, pin5, pin6, pin13, pin12, pin11, pin10, pin9, pin8
  Keyboard #(.trigger("falling")) keyboard_1 (
    .clk(CLK), .re(n7408_2_pin6), .data(keyboard_1_data));  // open: clr, avail
  _7408 #(.ShowInternalStructure("true"), .VccGndPorts("true")) u_7408_3 (
    .pin1(RAM_CS), .pin2(WR), .pin3(n7408_3_pin3), .pin4(RAM_CS), .pin5(RD), .pin6(n7408_3_pin6), .pin7(lo),
    .pin14(hi));  // open: pin13, pin12, pin11, pin10, pin9, pin8
  ROM #(.addrWidth(13)) rom_1 (.addr(A[12:0]), .data(rom_1_data));
  assign D = n7408_2_pin6 ? {1'b0, keyboard_1_data} : 8'bz;  // Controlled_Buffer controlled_buffer_1
  RAM #(.addrWidth(15)) ram_1 (.addr(A[14:0]), .we(n7408_3_pin3), .clk(CLK), .din(D), .dout(ram_1_dout));  // open: oe
  assign D = n7408_4_pin3 ? rom_1_data : 8'bz;  // Controlled_Buffer controlled_buffer_2
  _7408 #(.ShowInternalStructure("true"), .VccGndPorts("true")) u_7408_4 (
    .pin1(ROM_CS), .pin2(RD), .pin3(n7408_4_pin3), .pin7(lo), .pin14(hi));  // open: pin4, pin5, pin6, pin13, pin12, pin11, pin10, pin9, pin8
  assign D = n7408_3_pin6 ? ram_1_dout : 8'bz;  // Controlled_Buffer controlled_buffer_3
  // also tied to GND on the sheet: lo
  // also tied to VCC on the sheet: hi

  // Notes on the sheet:
  //   contents of rom_1 (hex, n*v repeats v):
  //   a9 8b 85 2 a9 e2 85 3 20 e e0 4c 1c e0 a0 0 b1 2 f0 7 8d 0 80 c8 4c 10 e0 60 20 7e e2 a9 0 a9 3f 8d
  //   0 80 a0 0 ad 1 80 f0 fb c9 a f0 1c c9 8 f0 e 99 4 0 8d 0 80 c8 c0 30 f0 dc 4c 28 e0 8d 0 80 88 10 df
  //   c8 4c 28 e0 8d 0 80 a0 0 20 79 e2 c9 20 f0 f9 c9 72 f0 f c9 77 f0 53 c9 65 f0 79 c9 68 f0 7b 4c 1c
  //   e0 20 bf e1 a9 1 85 3d a5 35 85 3b a5 36 85 3c e0 0 f0 7 20 bf e1 a5 35 85 3d a0 0 b1 3b aa 98 48 8a
  //   20 23 e2 aa 68 a8 8a c8 98 29 f d0 8 a9 a 8d 0 80 4c a8 e0 a9 20 8d 0 80 c4 3d d0 dc a9 a 8d 0 80 4c
  //   1c e0 20 bf e1 e0 0 d0 3 4c 1c e0 a5 35 85 3b a5 36 85 3c 84 3d a4 3d 20 bf e1 84 3d a0 0 a5 35 91
  //   3b e6 3b e0 0 d0 ed 4c 1c e0 20 bf e1 6c 35 0 a2 0 bd f5 e0 f0 7 8d 0 80 e8 4c e6 e0 4c 1c e0 48 6f
  //   77 20 74 6f 20 75 73 65 20 74 68 65 20 6d 6f 6e 69 74 6f 72 3a d a 20 20 2a 20 72 20 3c 61 64 64 72
  //   3e 20 5b 6e 5d 3a 20 50 72 69 6e 74 20 5b 6e 5d 20 62 79 74 65 73 20 66 72 6f 6d 20 3c 61 64 64 72
  //   3e d a 20 20 2a 20 77 20 3c 61 64 64 72 3e 20 5b 64 61 74 5d 3a 20 57 72 69 74 65 20 5b 64 61 74 5d
  //   20 74 6f 20 3c 61 64 64 72 3e d a 20 20 2a 20 65 20 3c 61 64 64 72 3e 3a 20 53 74 61 72 74 20 65 78
  //   65 63 75 74 69 6f 6e 20 61 74 20 3c 61 64 64 72 3e d a a 41 6c 6c 20 76 61 6c 75 65 73 20 6d 75 73
  //   74 20 62 65 20 77 72 69 74 74 65 6e 20 69 6e 20 68 65 78 61 64 65 63 69 6d 61 6c 2e d a 0 a9 0 85 35
  //   85 36 b9 4 0 c9 20 d0 6 20 79 e2 4c bf e1 a9 0 a2 0 20 79 e2 c9 0 f0 42 c9 20 f0 3c c9 30 30 3b f0 9
  //   c9 61 30 17 f0 8 4c fa e1 a9 0 4c 5 e2 a9 a 4c 5 e2 18 e9 61 69 a 4c 5 e2 38 e9 30 6 35 26 36 6 35
  //   26 36 6 35 26 36 6 35 26 36 18 5 35 85 35 4c d2 e1 a2 1 60 4c 1c e0 a2 1 a0 0 84 3a 84 37 84 38 c9 0
  //   f0 3f 4a 66 3a 4a 66 3a 4a 66 3a 4a 66 3a 18 66 3a 66 3a 66 3a 66 3a 18 a8 a5 3a c9 a 30 8 e9 a 18
  //   69 41 4c 58 e2 69 30 95 37 a9 0 85 3a ca 98 e0 ff d0 cd a9 37 85 2 a9 0 85 3 20 e e0 60 a9 30 8d 0
  //   80 8d 0 80 60 b9 4 0 c8 60 a0 0 a9 0 99 4 0 c8 c0 30 d0 f8 60 54 53 43 2d 38 20 52 4f 4d 20 76 30 2e
  //   31 20 4d 4c 20 4d 6f 6e 69 74 6f 72 2e d a 54 79 70 65 20 27 68 27 20 74 68 65 6e 20 65 6e 74 65 72
  //   20 66 6f 72 20 61 20 6c 69 73 74 20 6f 66 20 63 6f 6d 6d 61 6e 64 73 2e d a 7465*0 e0
endmodule

module nvram (
  input  a0,
  input  a1,
  input  a2,
  input  a3,
  input  a4,
  input  a5,
  input  a6,
  input  a7,
  input  a8,
  input  a9,
  input  a10,
  input  a11,
  input  a12,
  input  a13,
  input  a14,
  input  VCC,
  input  VSS,
  input  E,
  input  W,
  input  G,
  input  C,
  input  [7:0] D,
  output DQ0,
  output DQ1,
  output DQ2,
  output DQ3,
  output DQ4,
  output DQ5,
  output DQ6,
  output DQ7
);

  wire and_1_out, and_2_out, not_1_out, not_2_out, not_3_out;
  wire [7:0] ram_1_dout;

  not not_1 (not_1_out, E);
  not not_2 (not_2_out, W);
  not not_3 (not_3_out, G);
  and and_1 (and_1_out, not_1_out, not_2_out);
  and and_2 (and_2_out, not_1_out, not_3_out);
  RAM #(.addrWidth(15)) ram_1 (
    .addr({a14, a13, a12, a11, a10, a9, a8, a7, a6, a5, a4, a3, a2, a1, a0}), .we(and_1_out), .oe(and_2_out),
    .clk(C), .din(D), .dout(ram_1_dout));
  assign {DQ7, DQ6, DQ5, DQ4, DQ3, DQ2, DQ1, DQ0} = and_2_out ? ram_1_dout : 8'bz;  // Controlled_Buffer controlled_buffer_1
endmodule

module romic (
  input  a0,
  input  a1,
  input  a2,
  input  a3,
  input  a4,
  input  a5,
  input  a6,
  input  a7,
  input  a8,
  input  a9,
  input  a10,
  input  a11,
  input  a12,
  input  vcc,
  input  gnd,
  input  we,
  input  oe,
  input  ce,
  output io0,
  output io1,
  output io2,
  output io3,
  output io4,
  output io5,
  output io6,
  output io7
);

  wire and_1_out, not_2_out, not_3_out;
  wire [7:0] rom_1_data;

  // NOT_Gate not_1 has open pins: in=we, out=open
  not not_2 (not_2_out, oe);
  and and_1 (and_1_out, not_2_out, not_3_out);
  not not_3 (not_3_out, ce);
  ROM #(.addrWidth(13)) rom_1 (.addr({a12, a11, a10, a9, a8, a7, a6, a5, a4, a3, a2, a1, a0}), .data(rom_1_data));
  assign {io7, io6, io5, io4, io3, io2, io1, io0} = and_1_out ? rom_1_data : 8'bz;  // Controlled_Buffer controlled_buffer_1

  // Notes on the sheet:
  //   contents of rom_1 (hex, n*v repeats v):
  //   a9 1c 85 2 a9 e0 85 3 20 e e0 4c 66 e0 a0 0 b1 2 f0 7 8d 0 80 c8 4c 10 e0 60 54 53 43 2d 38 20 52 4f
  //   4d 20 76 30 2e 31 20 4d 4c 20 4d 6f 6e 69 74 6f 72 2e d a 54 79 70 65 20 27 68 27 20 74 68 65 6e 20
  //   65 6e 74 65 72 20 66 6f 72 20 61 20 6c 69 73 74 20 6f 66 20 63 6f 6d 6d 61 6e 64 73 2e d a 0 20 c8
  //   e2 a9 0 a9 3f 8d 0 80 a0 0 ad 1 80 f0 fb c9 a f0 1c c9 8 f0 e 99 4 0 8d 0 80 c8 c0 30 f0 dc 4c 72 e0
  //   8d 0 80 88 10 df c8 4c 72 e0 8d 0 80 a0 0 20 c3 e2 c9 20 f0 f9 c9 72 f0 f c9 77 f0 53 c9 65 f0 79 c9
  //   68 f0 7b 4c 66 e0 20 9 e2 a9 1 85 3d a5 35 85 3b a5 36 85 3c e0 0 f0 7 20 9 e2 a5 35 85 3d a0 0 b1
  //   3b aa 98 48 8a 20 6d e2 aa 68 a8 8a c8 98 29 f d0 8 a9 a 8d 0 80 4c f2 e0 a9 20 8d 0 80 c4 3d d0 dc
  //   a9 a 8d 0 80 4c 66 e0 20 9 e2 e0 0 d0 3 4c 66 e0 a5 35 85 3b a5 36 85 3c 84 3d a4 3d 20 9 e2 84 3d
  //   a0 0 a5 35 91 3b e6 3b e0 0 d0 ed 4c 66 e0 20 9 e2 6c 35 0 a2 0 bd 3f e1 f0 7 8d 0 80 e8 4c 30 e1 4c
  //   66 e0 48 6f 77 20 74 6f 20 75 73 65 20 74 68 65 20 6d 6f 6e 69 74 6f 72 3a d a 20 20 2a 20 72 20 3c
  //   61 64 64 72 3e 20 5b 6e 5d 3a 20 50 72 69 6e 74 20 5b 6e 5d 20 62 79 74 65 73 20 66 72 6f 6d 20 3c
  //   61 64 64 72 3e d a 20 20 2a 20 77 20 3c 61 64 64 72 3e 20 5b 64 61 74 5d 3a 20 57 72 69 74 65 20 5b
  //   64 61 74 5d 20 74 6f 20 3c 61 64 64 72 3e d a 20 20 2a 20 65 20 3c 61 64 64 72 3e 3a 20 53 74 61 72
  //   74 20 65 78 65 63 75 74 69 6f 6e 20 61 74 20 3c 61 64 64 72 3e d a a 41 6c 6c 20 76 61 6c 75 65 73
  //   20 6d 75 73 74 20 62 65 20 77 72 69 74 74 65 6e 20 69 6e 20 68 65 78 61 64 65 63 69 6d 61 6c 2e d a
  //   0 a9 0 85 35 85 36 b9 4 0 c9 20 d0 6 20 c3 e2 4c 9 e2 a9 0 a2 0 20 c3 e2 c9 0 f0 42 c9 20 f0 3c c9
  //   30 30 3b f0 9 c9 61 30 17 f0 8 4c 44 e2 a9 0 4c 4f e2 a9 a 4c 4f e2 18 e9 61 69 a 4c 4f e2 38 e9 30
  //   6 35 26 36 6 35 26 36 6 35 26 36 6 35 26 36 18 5 35 85 35 4c 1c e2 a2 1 60 4c 66 e0 a2 1 a0 0 84 3a
  //   84 37 84 38 c9 0 f0 3f 4a 66 3a 4a 66 3a 4a 66 3a 4a 66 3a 18 66 3a 66 3a 66 3a 66 3a 18 a8 a5 3a c9
  //   a 30 8 e9 a 18 69 41 4c a2 e2 69 30 95 37 a9 0 85 3a ca 98 e0 ff d0 cd a9 37 85 2 a9 0 85 3 20 e e0
  //   60 a9 30 8d 0 80 8d 0 80 60 b9 4 0 c8 60 a0 0 a9 0 99 4 0 c8 c0 30 d0 f8 60 0 0 0 e0
endmodule
